# Fritzing sketch arduino_morse_code_schematic (saved by Fritzing 0.9.3b)
breadboards: 1

parts:
  S1 = Pushbutton [package="[THT]"]
  S2 = Pushbutton [package="[THT]"]
  S3 = Pushbutton [package="[THT]"]
  S4 = Pushbutton [package="[THT]"]
  LED1 = smd LED [color="Red (633nm)" package="1206 [SMD]"]
  LED2 = smd LED [color="Green (565nm)" package="1206 [SMD]"]
  LED3 = smd LED [color="Blue (525nm)" package="1206 [SMD]"]
  R1 = Resistor [tolerance=±5% resistance=220 package="0402 [SMD]"]
  R2 = Resistor [tolerance=±5% resistance=220 package="0402 [SMD]"]
  R3 = Resistor [tolerance=±5% resistance=220 package="0402 [SMD]"]
  R4 = Resistor [tolerance=±5% resistance=220 package="0402 [SMD]"]
  R5 = Resistor [tolerance=±5% resistance=220 package="0402 [SMD]"]
  R6 = Resistor [tolerance=±5% resistance=220 package="0402 [SMD]"]
  S5 = Pushbutton [package="[THT]"]
  R7 = Resistor [tolerance=±5% resistance=220 package="0402 [SMD]"]
  R8 = Resistor [tolerance=±5% resistance=220 package="0402 [SMD]"]
  Part1 = Arduino Uno (Rev3) - ICSP
  J1 = Piezo Speaker

nets:
  N1: S1.Pin_1, S1.Pin_2, S1.Pin_3, S1.Pin_4, S2.Pin_1, S2.Pin_2, S2.Pin_3, S2.Pin_4, S3.Pin_3, S3.Pin_4, S4.Pin_1, S4.Pin_2, S4.Pin_3, S4.Pin_4, R2.Pin_0, R3.Pin_0, R4.Pin_0, R6.Pin_0, S5.Pin_1, S5.Pin_2, S5.Pin_3, S5.Pin_4, Part1.5V
  N2: S3.Pin_1, S3.Pin_2, LED1.cathode, LED2.cathode, LED3.cathode, R1.Pin_0, Part1.GND, J1.pin1
  N3: LED1.anode, R8.Pin_0
  N4: LED2.anode, R7.Pin_0
  N5: LED3.anode, R5.Pin_0
  N6: R1.Pin_1, Part1.D9_PWM
  N7: R2.Pin_1, Part1.D8
  N8: R3.Pin_1, Part1.D7
  N9: R4.Pin_1, Part1.D5_PWM
  N10: R5.Pin_1, Part1.D4
  N11: R6.Pin_1, Part1.D6_PWM
  N12: R7.Pin_1, Part1.D3_PWM
  N13: R8.Pin_1, Part1.D2
  N14: Part1.D10_PWM/SS, J1.pin2
